# Fritzing sketch Simulasi Fritzing (saved by Fritzing 0.9.5d)

parts:
  DS1 = DS18B20 1-Wire Temperature Sensor [part_number=DS18B20]
  MAX30100_Sensor1 = MAX30100 Oximeter and Heart-Rate Sensor [part_number=MAX30100]
  Grove1 = Grove OLED 128x96
  Part1 = Arduino Uno (Rev3) - ICSP

nets:
  GND: DS1.GND, MAX30100_Sensor1.GND, Grove1.GND, Part1.GND
  N1: DS1.DQ, Part1.D2
  VDD: DS1.VDD, Grove1.VCC, Part1.5V
  VIN: MAX30100_Sensor1.VIN, Part1.3V3
  N2: MAX30100_Sensor1.SCL, Grove1.SCL, Part1.A5/SCL
  N3: MAX30100_Sensor1.SDA, Grove1.SDA, Part1.A4/SDA

custom parts:
  MAX30100 Oximeter and Heart-Rate Sensor: The MAX30100 is an integrated pulse oximetry and heart-rate monitor biosensor module. It includes internal LEDs, photodetectors, optical elements, and low-noise electronics with ambient light rejection. The MAX30100 operates on a single 1.8V power supply and a separate 3.3V power supply for the internal LEDs. Communication is through a I2C-compatible interface.

// code stored in the sketch: sketch_apr20a_copy_20250420230958.ino
#include <Wire.h>
#include <Adafruit_GFX.h>
#include <Adafruit_SSD1306.h>
#include <DallasTemperature.h>
#include <OneWire.h>
#include "MAX30100_PulseOximeter.h"

#define SCREEN_WIDTH 128
#define SCREEN_HEIGHT 64
Adafruit_SSD1306 display(SCREEN_WIDTH, SCREEN_HEIGHT, &Wire, -1);

// DS18B20 setup
#define ONE_WIRE_BUS 2
OneWire oneWire(ONE_WIRE_BUS);
DallasTemperature sensors(&oneWire);

// MAX30100 setup
PulseOximeter pox;
uint32_t lastReport = 0;
float bpm = 0;
float spo2 = 0;

void onBeatDetected() {
  Serial.println("Detak terdeteksi!");
}

void setup() {
  Serial.begin(9600);
  sensors.begin();

  // OLED
  if (!display.begin(SSD1306_SWITCHCAPVCC, 0x3C)) {
    Serial.println("OLED gagal");
    while (1);
  }

  display.clearDisplay();
  display.setTextSize(1);
  display.setTextColor(SSD1306_WHITE);

  // MAX30100
  if (!pox.begin()) {
    Serial.println("Sensor MAX30100 gagal");
    while (1);
  } else {
    Serial.println("Sensor MAX30100 berhasil");
  }

  pox.setOnBeatDetectedCallback(onBeatDetected);
}

void loop() {
  pox.update(); // Update data dari MAX30100

  // Ambil data suhu
  sensors.requestTemperatures();
  float suhu = sensors.getTempCByIndex(0);

  // Ambil BPM dan SpO2
  bpm = pox.getHeartRate();
  spo2 = pox.getSpO2();

  // Tampilkan di OLED
  display.clearDisplay();
  display.setCursor(0, 0);
  display.println("Monitoring Kesehatan");
  display.println("---------------------");

  display.print("Suhu: ");
  display.print(suhu);
  display.println(" C");

  display.print("BPM: ");
  if (bpm > 0) {
    display.print(bpm);
  } else {
    display.print("Mengukur...");
  }

  display.display();

  delay(1000); // Delay 1 detik
}
